// Logisim project CircuitProject.circ as structural Verilog: 4 circuits, main circuit main
module main (
  input  SW14,
  input  SW13,
  input  SW12,
  input  SW11,
  input  SW10,
  input  SW9,
  input  SW8,
  input  SW15,
  input  SW6,
  input  SW5,
  input  SW4,
  input  SW3,
  input  SW2,
  input  SW1,
  input  SW0,
  input  SW7,
  output [15:0] out_17,
  output z1,
  output z0
);

  wire and_1_out, and_2_out, and_3_out, and_4_out, and_5_out, and_6_out, and_7_out, and_8_out, and_9_out,
       and_10_out, BTNL_out, BTNR_out, clk_out, custom_7_segment_decoder_1_a, custom_7_segment_decoder_1_b,
       custom_7_segment_decoder_1_c, custom_7_segment_decoder_1_d, custom_7_segment_decoder_1_e,
       custom_7_segment_decoder_1_f, custom_7_segment_decoder_1_g, custom_7_segment_decoder_2_a,
       custom_7_segment_decoder_2_b, custom_7_segment_decoder_2_c, custom_7_segment_decoder_2_d,
       custom_7_segment_decoder_2_e, custom_7_segment_decoder_2_f, custom_7_segment_decoder_2_g,
       custom_7_segment_decoder_3_a, custom_7_segment_decoder_3_b, custom_7_segment_decoder_3_c,
       custom_7_segment_decoder_3_d, custom_7_segment_decoder_3_e, custom_7_segment_decoder_3_f,
       custom_7_segment_decoder_3_g, nor_1_out, not_1_out, not_2_out, not_3_out, not_4_out, not_5_out,
       not_6_out, or_1_out, or_2_out, or_3_out, or_4_out, or_5_out, or_6_out, or_7_out, or_8_out, or_9_out,
       or_10_out, or_11_out, or_12_out, or_13_out, register_1_q, shift_register_1_p1, shift_register_2_p23,
       shift_register_2_p24, shift_register_2_p25, shift_register_2_p26, shift_register_2_p27,
       shift_register_2_p28, shift_register_2_p29, shift_register_2_p30, xor_1_out, y0_qn, y1_qn;
  wire [1:0] multiplexer_4_out;
  wire [3:0] binary16bittobcd_1_bcd_1s, binary16bittobcd_1_bcd_10s, binary16bittobcd_1_bcd_100s,
       binary16bittobcd_1_bcd_1000s, binary16bittobcd_1_bcd_10000s, multiplexer_5_out, multiplexer_6_out,
       multiplexer_7_out;
  wire [6:0] multiplexer_8_out;
  wire [7:0] multiplexer_1_out, multiplexer_2_out;
  wire [7:1] xor_2_out, xor_9_out;
  wire [15:0] adder_1_out, multiplexer_3_out, shift_register_1_p14;

  Clock clk (.out(clk_out));
  or or_1 (or_1_out, SW11, or_5_out);
  or or_2 (or_2_out, SW12, or_1_out);
  or or_3 (or_3_out, SW13, or_2_out);
  or or_4 (or_4_out, SW9, SW8);
  or or_5 (or_5_out, SW10, or_4_out);
  or or_6 (or_6_out, SW4, or_10_out);
  or or_7 (or_7_out, SW5, or_6_out);
  Register #(.width(1)) register_1 (
    .D(xor_1_out), .en(shift_register_1_p1), .clk(clk_out), .Q(register_1_q));  // open: clr
  xor xor_1 (xor_1_out, SW7, SW15);
  xor xor_2 (xor_2_out[1], SW8, SW9);
  xor xor_3 (xor_2_out[2], or_4_out, SW10);
  xor xor_4 (xor_2_out[3], or_5_out, SW11);
  xor xor_5 (xor_2_out[4], or_1_out, SW12);
  xor xor_6 (xor_2_out[5], or_2_out, SW13);
  xor xor_7 (xor_2_out[6], or_3_out, SW14);
  xor xor_8 (xor_2_out[7], or_3_out, SW15);
  or or_8 (or_8_out, SW1, SW0);
  or or_9 (or_9_out, SW2, or_8_out);
  or or_10 (or_10_out, SW3, or_9_out);
  xor xor_9 (xor_9_out[1], SW0, SW1);
  xor xor_10 (xor_9_out[2], or_8_out, SW2);
  xor xor_11 (xor_9_out[3], or_9_out, SW3);
  xor xor_12 (xor_9_out[4], or_10_out, SW4);
  xor xor_13 (xor_9_out[5], or_6_out, SW5);
  xor xor_14 (xor_9_out[6], or_7_out, SW6);
  xor xor_15 (xor_9_out[7], or_7_out, SW7);
  Multiplexer #(.width(8)) multiplexer_1 (
    .in0({SW15, SW14, SW13, SW12, SW11, SW10, SW9, SW8}), .in1({xor_2_out, SW8}), .out(multiplexer_1_out),
    .sel(SW15));
  not not_1 (not_1_out, shift_register_1_p1);
  not not_2 (not_2_out, shift_register_1_p1);
  Multiplexer #(.width(8)) multiplexer_2 (
    .in0({SW7, SW6, SW5, SW4, SW3, SW2, SW1, SW0}), .in1({xor_9_out, SW0}), .out(multiplexer_2_out), .sel(SW7));
  // Shift_Register #(.length(16)) shift_register_1: pin names not known; wires that end beside it: shift_register_1_p1, not_1_out, clk_out, 1'b0, multiplexer_1_out[0], multiplexer_1_out[1], multiplexer_1_out[2], multiplexer_1_out[3], multiplexer_1_out[4], multiplexer_1_out[5], multiplexer_1_out[6], multiplexer_1_out[7], 1'b0, shift_register_1_p14[0], shift_register_1_p14[1], shift_register_1_p14[2], shift_register_1_p14[3], shift_register_1_p14[4], shift_register_1_p14[5], shift_register_1_p14[6]
  // Shift_Register shift_register_2: pin names not known; wires that end beside it: 1'b0, shift_register_1_p1, not_2_out, clk_out, 1'b0, multiplexer_2_out[7], multiplexer_2_out[6], multiplexer_2_out[5], multiplexer_2_out[4], multiplexer_2_out[3], multiplexer_2_out[2], multiplexer_2_out[1], multiplexer_2_out[0], shift_register_1_p14[7], shift_register_1_p14[8], shift_register_1_p14[9], shift_register_1_p14[10], shift_register_1_p14[11], shift_register_1_p14[12], shift_register_1_p14[13], shift_register_1_p14[14], shift_register_1_p14[15], shift_register_2_p23, shift_register_2_p24, shift_register_2_p25, shift_register_2_p26, shift_register_2_p27, shift_register_2_p28, shift_register_2_p29, shift_register_2_p30
  nor nor_1 (nor_1_out, shift_register_2_p23, shift_register_2_p24, shift_register_2_p25, shift_register_2_p26, shift_register_2_p27, shift_register_2_p28, shift_register_2_p29, shift_register_2_p30);
  not not_3 (not_3_out, shift_register_1_p1);
  Adder #(.width(16)) adder_1 (.a(out_17), .b(shift_register_1_p14), .out(adder_1_out), .cin(1'b0));  // open: cout
  Button BTNC (.out(shift_register_1_p1));
  Register #(.width(16)) register_2 (.D(multiplexer_3_out), .en(or_11_out), .clk(clk_out), .Q(out_17));  // open: clr
  Multiplexer #(.width(16)) multiplexer_3 (
    .in0({16{1'b0}}), .in1(adder_1_out), .out(multiplexer_3_out), .sel(not_3_out));
  or or_11 (or_11_out, not_4_out, shift_register_2_p30);
  not not_4 (not_4_out, not_3_out);
  Button BTNL (.out(BTNL_out));
  Button BTNR (.out(BTNR_out));
  not not_5 (not_5_out, BTNL_out);
  not not_6 (not_6_out, BTNR_out);
  and and_1 (and_1_out, z1, z0);
  and and_2 (and_2_out, y0_qn, BTNL_out);
  and and_3 (and_3_out, BTNL_out, not_6_out);
  and and_4 (and_4_out, not_6_out, y0_qn);
  and and_5 (and_5_out, y1_qn, BTNR_out);
  and and_6 (and_6_out, y0_qn, BTNR_out, not_5_out);
  and and_7 (and_7_out, y0_qn, and_3_out);
  and and_8 (and_8_out, not_6_out, not_5_out, z0);
  and and_9 (and_9_out, and_1_out, BTNL_out);
  binary16bitToBCD binary16bittobcd_1 (
    .Binary_16bit(out_17), .BCD_1s(binary16bittobcd_1_bcd_1s), .BCD_10s(binary16bittobcd_1_bcd_10s),
    .BCD_100s(binary16bittobcd_1_bcd_100s), .BCD_1000s(binary16bittobcd_1_bcd_1000s),
    .BCD_10000s(binary16bittobcd_1_bcd_10000s));
  or or_12 (or_12_out, and_1_out, and_2_out, and_3_out, and_4_out);
  or or_13 (or_13_out, and_5_out, and_6_out, and_7_out, and_8_out, and_9_out);
  D_Flip_Flop y1 (.D(or_12_out), .clk(clk_out), .Q(z1), .Qn(y1_qn));  // open: preset, reset
  D_Flip_Flop y0 (.D(or_13_out), .clk(clk_out), .Q(z0), .Qn(y0_qn));  // open: preset, reset
  Multiplexer #(.width(2)) multiplexer_4 (.in0(2'b00), .in1({z1, z0}), .out(multiplexer_4_out), .sel(and_10_out));
  and and_10 (and_10_out, nor_1_out, not_3_out);
  Multiplexer #(.select(2), .width(4)) multiplexer_5 (
    .in0(4'b1111), .in1(binary16bittobcd_1_bcd_1s), .in2(binary16bittobcd_1_bcd_10s),
    .in3(binary16bittobcd_1_bcd_100s), .out(multiplexer_5_out), .sel(multiplexer_4_out));
  Multiplexer #(.select(2), .width(4)) multiplexer_6 (
    .in0(4'b1111), .in1(binary16bittobcd_1_bcd_10s), .in2(binary16bittobcd_1_bcd_100s),
    .in3(binary16bittobcd_1_bcd_1000s), .out(multiplexer_6_out), .sel(multiplexer_4_out));
  Multiplexer #(.select(2), .width(4)) multiplexer_7 (
    .in0(4'b1111), .in1(binary16bittobcd_1_bcd_100s), .in2(binary16bittobcd_1_bcd_1000s),
    .in3(binary16bittobcd_1_bcd_10000s), .out(multiplexer_7_out), .sel(multiplexer_4_out));
  Custom_7_Segment_Decoder custom_7_segment_decoder_1 (
    .dataIn(multiplexer_7_out), .a(custom_7_segment_decoder_1_a), .b(custom_7_segment_decoder_1_b),
    .c(custom_7_segment_decoder_1_c), .d(custom_7_segment_decoder_1_d), .e(custom_7_segment_decoder_1_e),
    .f(custom_7_segment_decoder_1_f), .g(custom_7_segment_decoder_1_g));
  Custom_7_Segment_Decoder custom_7_segment_decoder_2 (
    .dataIn(multiplexer_6_out), .a(custom_7_segment_decoder_2_a), .b(custom_7_segment_decoder_2_b),
    .c(custom_7_segment_decoder_2_c), .d(custom_7_segment_decoder_2_d), .e(custom_7_segment_decoder_2_e),
    .f(custom_7_segment_decoder_2_f), .g(custom_7_segment_decoder_2_g));
  Multiplexer #(.width(7)) multiplexer_8 (
    .in0({7{1'b1}}), .in1(7'b0111111), .out(multiplexer_8_out), .sel(register_1_q));
  Custom_7_Segment_Decoder custom_7_segment_decoder_3 (
    .dataIn(multiplexer_5_out), .a(custom_7_segment_decoder_3_a), .b(custom_7_segment_decoder_3_b),
    .c(custom_7_segment_decoder_3_c), .d(custom_7_segment_decoder_3_d), .e(custom_7_segment_decoder_3_e),
    .f(custom_7_segment_decoder_3_f), .g(custom_7_segment_decoder_3_g));
  _7_Segment_Display #(.active("false")) u_7_segment_display_1 (
    .g(multiplexer_8_out[6]), .f(multiplexer_8_out[5]), .a(multiplexer_8_out[0]), .b(multiplexer_8_out[1]),
    .e(multiplexer_8_out[4]), .d(multiplexer_8_out[3]), .c(multiplexer_8_out[2]), .dp(1'b1));
  _7_Segment_Display #(.active("false"), .decimalPoint("false")) u_7_segment_display_2 (
    .g(custom_7_segment_decoder_1_g), .f(custom_7_segment_decoder_1_f), .a(custom_7_segment_decoder_1_a),
    .b(custom_7_segment_decoder_1_b), .e(custom_7_segment_decoder_1_e), .d(custom_7_segment_decoder_1_d),
    .c(custom_7_segment_decoder_1_c));
  _7_Segment_Display #(.active("false"), .decimalPoint("false")) u_7_segment_display_3 (
    .g(custom_7_segment_decoder_2_g), .f(custom_7_segment_decoder_2_f), .a(custom_7_segment_decoder_2_a),
    .b(custom_7_segment_decoder_2_b), .e(custom_7_segment_decoder_2_e), .d(custom_7_segment_decoder_2_d),
    .c(custom_7_segment_decoder_2_c));
  _7_Segment_Display #(.active("false"), .decimalPoint("false")) u_7_segment_display_4 (
    .g(custom_7_segment_decoder_3_g), .f(custom_7_segment_decoder_3_f), .a(custom_7_segment_decoder_3_a),
    .b(custom_7_segment_decoder_3_b), .e(custom_7_segment_decoder_3_e), .d(custom_7_segment_decoder_3_d),
    .c(custom_7_segment_decoder_3_c));

  // Notes on the sheet:
  //   LI
  //   LI (bar)
  //   LI
  //   LI
  //   LI (bar)
  //   b0
  //   LI (bar)
  //   Z
  //   Lp
  //   Z_flag
  //   BTNC (bar)
  //   DS
endmodule

module Custom_7_Segment_Decoder (
  input  [3:0] dataIn,
  output a,
  output b,
  output c,
  output d,
  output e,
  output f,
  output g
);

  wire and_1_out, and_2_out, and_3_out, and_4_out, and_5_out, and_6_out, and_7_out, and_8_out, and_9_out,
       and_10_out, and_11_out, and_12_out, and_13_out, and_14_out, and_15_out, and_16_out, and_17_out,
       not_1_out, not_2_out, not_3_out, not_4_out;

  not not_1 (not_1_out, dataIn[3]);
  not not_2 (not_2_out, dataIn[2]);
  not not_3 (not_3_out, dataIn[1]);
  not not_4 (not_4_out, dataIn[0]);
  and and_1 (and_1_out, not_1_out, not_2_out, not_3_out, dataIn[0]);
  and and_2 (and_2_out, dataIn[2], not_3_out, not_4_out);
  and and_3 (and_3_out, dataIn[3], dataIn[1]);
  and and_4 (and_4_out, dataIn[2], not_3_out, dataIn[0]);
  and and_5 (and_5_out, dataIn[2], dataIn[1], not_4_out);
  and and_6 (and_6_out, dataIn[3], dataIn[1]);
  and and_7 (and_7_out, not_2_out, dataIn[1], not_4_out);
  and and_8 (and_8_out, dataIn[3], dataIn[1]);
  and and_9 (and_9_out, not_1_out, not_2_out, not_3_out, dataIn[0]);
  and and_10 (and_10_out, dataIn[2], not_3_out, not_4_out);
  and and_11 (and_11_out, not_1_out, dataIn[2], dataIn[1], dataIn[0]);
  and and_12 (and_12_out, dataIn[2], not_3_out);
  and and_13 (and_13_out, not_1_out, not_2_out, dataIn[0]);
  and and_14 (and_14_out, not_2_out, dataIn[1]);
  and and_15 (and_15_out, dataIn[1], dataIn[0]);
  and and_16 (and_16_out, not_1_out, not_2_out, not_3_out);
  and and_17 (and_17_out, dataIn[2], dataIn[1], dataIn[0]);
  or or_1 (a, and_1_out, and_2_out, and_3_out);
  or or_2 (b, and_4_out, and_5_out, and_6_out);
  or or_3 (c, and_7_out, and_8_out);
  or or_4 (d, and_9_out, and_10_out, and_11_out);
  or or_5 (e, dataIn[0], and_12_out);
  or or_6 (f, and_13_out, and_14_out, and_15_out);
  or or_7 (g, and_16_out, and_17_out);
endmodule

module greaterThan4Add3 (
  input  in_0,
  input  in_1,
  input  in_2,
  input  in_3,
  output output_0,
  output output_1,
  output output_2,
  output output_3
);

  wire comparator_1_gt;
  wire [3:0] adder_1_out;

  Adder #(.width(4)) adder_1 (.a(4'b0011), .b({in_3, in_2, in_1, in_0}), .out(adder_1_out));  // open: cin, cout
  Multiplexer #(.width(4)) multiplexer_1 (
    .in0({in_3, in_2, in_1, in_0}), .in1(adder_1_out), .out({output_3, output_2, output_1, output_0}),
    .sel(comparator_1_gt));
  Comparator #(.mode("unsigned"), .width(4)) comparator_1 (
    .a({in_3, in_2, in_1, in_0}), .b(4'b0100), .gt(comparator_1_gt));  // open: eq, lt
endmodule

module binary16bitToBCD (
  input  [15:0] Binary_16bit,
  output [3:0] BCD_1s,
  output [3:0] BCD_10s,
  output [3:0] BCD_100s,
  output [3:0] BCD_1000s,
  output [3:0] BCD_10000s
);

  wire greaterthan4add3_1_output_0, greaterthan4add3_1_output_1, greaterthan4add3_1_output_2,
       greaterthan4add3_1_output_3, greaterthan4add3_2_output_0, greaterthan4add3_2_output_1,
       greaterthan4add3_2_output_2, greaterthan4add3_2_output_3, greaterthan4add3_3_output_0,
       greaterthan4add3_3_output_1, greaterthan4add3_3_output_2, greaterthan4add3_3_output_3,
       greaterthan4add3_4_output_0, greaterthan4add3_4_output_1, greaterthan4add3_4_output_2,
       greaterthan4add3_4_output_3, greaterthan4add3_5_output_0, greaterthan4add3_5_output_1,
       greaterthan4add3_5_output_2, greaterthan4add3_5_output_3, greaterthan4add3_6_output_0,
       greaterthan4add3_6_output_1, greaterthan4add3_6_output_2, greaterthan4add3_6_output_3,
       greaterthan4add3_7_output_0, greaterthan4add3_7_output_1, greaterthan4add3_7_output_2,
       greaterthan4add3_7_output_3, greaterthan4add3_8_output_0, greaterthan4add3_8_output_1,
       greaterthan4add3_8_output_2, greaterthan4add3_8_output_3, greaterthan4add3_9_output_0,
       greaterthan4add3_9_output_1, greaterthan4add3_9_output_2, greaterthan4add3_9_output_3,
       greaterthan4add3_10_output_0, greaterthan4add3_10_output_1, greaterthan4add3_10_output_2,
       greaterthan4add3_10_output_3, greaterthan4add3_11_output_0, greaterthan4add3_11_output_1,
       greaterthan4add3_11_output_2, greaterthan4add3_11_output_3, greaterthan4add3_12_output_0,
       greaterthan4add3_12_output_1, greaterthan4add3_12_output_2, greaterthan4add3_12_output_3,
       greaterthan4add3_13_output_0, greaterthan4add3_13_output_1, greaterthan4add3_13_output_2,
       greaterthan4add3_13_output_3, greaterthan4add3_14_output_0, greaterthan4add3_14_output_1,
       greaterthan4add3_14_output_2, greaterthan4add3_14_output_3, greaterthan4add3_15_output_0,
       greaterthan4add3_15_output_1, greaterthan4add3_15_output_2, greaterthan4add3_15_output_3,
       greaterthan4add3_16_output_0, greaterthan4add3_16_output_1, greaterthan4add3_16_output_2,
       greaterthan4add3_16_output_3, greaterthan4add3_17_output_0, greaterthan4add3_17_output_1,
       greaterthan4add3_17_output_2, greaterthan4add3_17_output_3, greaterthan4add3_18_output_0,
       greaterthan4add3_18_output_1, greaterthan4add3_18_output_2, greaterthan4add3_18_output_3,
       greaterthan4add3_19_output_0, greaterthan4add3_19_output_1, greaterthan4add3_19_output_2,
       greaterthan4add3_19_output_3, greaterthan4add3_20_output_0, greaterthan4add3_20_output_1,
       greaterthan4add3_20_output_2, greaterthan4add3_20_output_3, greaterthan4add3_21_output_0,
       greaterthan4add3_21_output_1, greaterthan4add3_21_output_2, greaterthan4add3_21_output_3,
       greaterthan4add3_22_output_0, greaterthan4add3_22_output_1, greaterthan4add3_22_output_2,
       greaterthan4add3_22_output_3, greaterthan4add3_23_output_0, greaterthan4add3_23_output_1,
       greaterthan4add3_23_output_2, greaterthan4add3_23_output_3, greaterthan4add3_24_output_0,
       greaterthan4add3_24_output_1, greaterthan4add3_24_output_2, greaterthan4add3_24_output_3,
       greaterthan4add3_25_output_0, greaterthan4add3_25_output_1, greaterthan4add3_25_output_2,
       greaterthan4add3_25_output_3, greaterthan4add3_26_output_0, greaterthan4add3_26_output_1,
       greaterthan4add3_26_output_2, greaterthan4add3_26_output_3, greaterthan4add3_27_output_0,
       greaterthan4add3_27_output_1, greaterthan4add3_27_output_2, greaterthan4add3_27_output_3,
       greaterthan4add3_28_output_0, greaterthan4add3_28_output_1, greaterthan4add3_28_output_2,
       greaterthan4add3_28_output_3, greaterthan4add3_29_output_0, greaterthan4add3_29_output_1,
       greaterthan4add3_29_output_2, greaterthan4add3_29_output_3, greaterthan4add3_30_output_0,
       greaterthan4add3_30_output_1, greaterthan4add3_30_output_2, greaterthan4add3_30_output_3;

  greaterThan4Add3 greaterthan4add3_1 (
    .in_0(Binary_16bit[13]), .in_1(Binary_16bit[14]), .in_2(Binary_16bit[15]), .in_3(1'b0),
    .output_0(greaterthan4add3_1_output_0), .output_1(greaterthan4add3_1_output_1),
    .output_2(greaterthan4add3_1_output_2), .output_3(greaterthan4add3_1_output_3));
  greaterThan4Add3 greaterthan4add3_2 (
    .in_0(Binary_16bit[12]), .in_1(greaterthan4add3_1_output_0), .in_2(greaterthan4add3_1_output_1),
    .in_3(greaterthan4add3_1_output_2), .output_0(greaterthan4add3_2_output_0),
    .output_1(greaterthan4add3_2_output_1), .output_2(greaterthan4add3_2_output_2),
    .output_3(greaterthan4add3_2_output_3));
  greaterThan4Add3 greaterthan4add3_3 (
    .in_0(Binary_16bit[11]), .in_1(greaterthan4add3_2_output_0), .in_2(greaterthan4add3_2_output_1),
    .in_3(greaterthan4add3_2_output_2), .output_0(greaterthan4add3_3_output_0),
    .output_1(greaterthan4add3_3_output_1), .output_2(greaterthan4add3_3_output_2),
    .output_3(greaterthan4add3_3_output_3));
  greaterThan4Add3 greaterthan4add3_4 (
    .in_0(Binary_16bit[10]), .in_1(greaterthan4add3_3_output_0), .in_2(greaterthan4add3_3_output_1),
    .in_3(greaterthan4add3_3_output_2), .output_0(greaterthan4add3_4_output_0),
    .output_1(greaterthan4add3_4_output_1), .output_2(greaterthan4add3_4_output_2),
    .output_3(greaterthan4add3_4_output_3));
  greaterThan4Add3 greaterthan4add3_5 (
    .in_0(greaterthan4add3_3_output_3), .in_1(greaterthan4add3_2_output_3),
    .in_2(greaterthan4add3_1_output_3), .in_3(1'b0), .output_0(greaterthan4add3_5_output_0),
    .output_1(greaterthan4add3_5_output_1), .output_2(greaterthan4add3_5_output_2),
    .output_3(greaterthan4add3_5_output_3));
  greaterThan4Add3 greaterthan4add3_6 (
    .in_0(Binary_16bit[9]), .in_1(greaterthan4add3_4_output_0), .in_2(greaterthan4add3_4_output_1),
    .in_3(greaterthan4add3_4_output_2), .output_0(greaterthan4add3_6_output_0),
    .output_1(greaterthan4add3_6_output_1), .output_2(greaterthan4add3_6_output_2),
    .output_3(greaterthan4add3_6_output_3));
  greaterThan4Add3 greaterthan4add3_7 (
    .in_0(greaterthan4add3_4_output_3), .in_1(greaterthan4add3_5_output_0),
    .in_2(greaterthan4add3_5_output_1), .in_3(greaterthan4add3_5_output_2),
    .output_0(greaterthan4add3_7_output_0), .output_1(greaterthan4add3_7_output_1),
    .output_2(greaterthan4add3_7_output_2), .output_3(greaterthan4add3_7_output_3));
  greaterThan4Add3 greaterthan4add3_8 (
    .in_0(Binary_16bit[8]), .in_1(greaterthan4add3_6_output_0), .in_2(greaterthan4add3_6_output_1),
    .in_3(greaterthan4add3_6_output_2), .output_0(greaterthan4add3_8_output_0),
    .output_1(greaterthan4add3_8_output_1), .output_2(greaterthan4add3_8_output_2),
    .output_3(greaterthan4add3_8_output_3));
  greaterThan4Add3 greaterthan4add3_9 (
    .in_0(greaterthan4add3_6_output_3), .in_1(greaterthan4add3_7_output_0),
    .in_2(greaterthan4add3_7_output_1), .in_3(greaterthan4add3_7_output_2),
    .output_0(greaterthan4add3_9_output_0), .output_1(greaterthan4add3_9_output_1),
    .output_2(greaterthan4add3_9_output_2), .output_3(greaterthan4add3_9_output_3));
  greaterThan4Add3 greaterthan4add3_10 (
    .in_0(Binary_16bit[7]), .in_1(greaterthan4add3_8_output_0), .in_2(greaterthan4add3_8_output_1),
    .in_3(greaterthan4add3_8_output_2), .output_0(greaterthan4add3_10_output_0),
    .output_1(greaterthan4add3_10_output_1), .output_2(greaterthan4add3_10_output_2),
    .output_3(greaterthan4add3_10_output_3));
  greaterThan4Add3 greaterthan4add3_11 (
    .in_0(greaterthan4add3_8_output_3), .in_1(greaterthan4add3_9_output_0),
    .in_2(greaterthan4add3_9_output_1), .in_3(greaterthan4add3_9_output_2),
    .output_0(greaterthan4add3_11_output_0), .output_1(greaterthan4add3_11_output_1),
    .output_2(greaterthan4add3_11_output_2), .output_3(greaterthan4add3_11_output_3));
  greaterThan4Add3 greaterthan4add3_12 (
    .in_0(greaterthan4add3_9_output_3), .in_1(greaterthan4add3_7_output_3),
    .in_2(greaterthan4add3_5_output_3), .in_3(1'b0), .output_0(greaterthan4add3_12_output_0),
    .output_1(greaterthan4add3_12_output_1), .output_2(greaterthan4add3_12_output_2),
    .output_3(greaterthan4add3_12_output_3));
  greaterThan4Add3 greaterthan4add3_13 (
    .in_0(Binary_16bit[6]), .in_1(greaterthan4add3_10_output_0), .in_2(greaterthan4add3_10_output_1),
    .in_3(greaterthan4add3_10_output_2), .output_0(greaterthan4add3_13_output_0),
    .output_1(greaterthan4add3_13_output_1), .output_2(greaterthan4add3_13_output_2),
    .output_3(greaterthan4add3_13_output_3));
  greaterThan4Add3 greaterthan4add3_14 (
    .in_0(greaterthan4add3_10_output_3), .in_1(greaterthan4add3_11_output_0),
    .in_2(greaterthan4add3_11_output_1), .in_3(greaterthan4add3_11_output_2),
    .output_0(greaterthan4add3_14_output_0), .output_1(greaterthan4add3_14_output_1),
    .output_2(greaterthan4add3_14_output_2), .output_3(greaterthan4add3_14_output_3));
  greaterThan4Add3 greaterthan4add3_15 (
    .in_0(greaterthan4add3_11_output_3), .in_1(greaterthan4add3_12_output_0),
    .in_2(greaterthan4add3_12_output_1), .in_3(greaterthan4add3_12_output_2),
    .output_0(greaterthan4add3_15_output_0), .output_1(greaterthan4add3_15_output_1),
    .output_2(greaterthan4add3_15_output_2), .output_3(greaterthan4add3_15_output_3));
  greaterThan4Add3 greaterthan4add3_16 (
    .in_0(Binary_16bit[5]), .in_1(greaterthan4add3_13_output_0), .in_2(greaterthan4add3_13_output_1),
    .in_3(greaterthan4add3_13_output_2), .output_0(greaterthan4add3_16_output_0),
    .output_1(greaterthan4add3_16_output_1), .output_2(greaterthan4add3_16_output_2),
    .output_3(greaterthan4add3_16_output_3));
  greaterThan4Add3 greaterthan4add3_17 (
    .in_0(greaterthan4add3_13_output_3), .in_1(greaterthan4add3_14_output_0),
    .in_2(greaterthan4add3_14_output_1), .in_3(greaterthan4add3_14_output_2),
    .output_0(greaterthan4add3_17_output_0), .output_1(greaterthan4add3_17_output_1),
    .output_2(greaterthan4add3_17_output_2), .output_3(greaterthan4add3_17_output_3));
  greaterThan4Add3 greaterthan4add3_18 (
    .in_0(greaterthan4add3_14_output_3), .in_1(greaterthan4add3_15_output_0),
    .in_2(greaterthan4add3_15_output_1), .in_3(greaterthan4add3_15_output_2),
    .output_0(greaterthan4add3_18_output_0), .output_1(greaterthan4add3_18_output_1),
    .output_2(greaterthan4add3_18_output_2), .output_3(greaterthan4add3_18_output_3));
  greaterThan4Add3 greaterthan4add3_19 (
    .in_0(Binary_16bit[4]), .in_1(greaterthan4add3_16_output_0), .in_2(greaterthan4add3_16_output_1),
    .in_3(greaterthan4add3_16_output_2), .output_0(greaterthan4add3_19_output_0),
    .output_1(greaterthan4add3_19_output_1), .output_2(greaterthan4add3_19_output_2),
    .output_3(greaterthan4add3_19_output_3));
  greaterThan4Add3 greaterthan4add3_20 (
    .in_0(greaterthan4add3_16_output_3), .in_1(greaterthan4add3_17_output_0),
    .in_2(greaterthan4add3_17_output_1), .in_3(greaterthan4add3_17_output_2),
    .output_0(greaterthan4add3_20_output_0), .output_1(greaterthan4add3_20_output_1),
    .output_2(greaterthan4add3_20_output_2), .output_3(greaterthan4add3_20_output_3));
  greaterThan4Add3 greaterthan4add3_21 (
    .in_0(greaterthan4add3_17_output_3), .in_1(greaterthan4add3_18_output_0),
    .in_2(greaterthan4add3_18_output_1), .in_3(greaterthan4add3_18_output_2),
    .output_0(greaterthan4add3_21_output_0), .output_1(greaterthan4add3_21_output_1),
    .output_2(greaterthan4add3_21_output_2), .output_3(greaterthan4add3_21_output_3));
  greaterThan4Add3 greaterthan4add3_22 (
    .in_0(greaterthan4add3_18_output_3), .in_1(greaterthan4add3_15_output_3),
    .in_2(greaterthan4add3_12_output_3), .in_3(1'b0), .output_0(greaterthan4add3_22_output_0),
    .output_1(greaterthan4add3_22_output_1), .output_2(greaterthan4add3_22_output_2),
    .output_3(greaterthan4add3_22_output_3));
  greaterThan4Add3 greaterthan4add3_23 (
    .in_0(Binary_16bit[3]), .in_1(greaterthan4add3_19_output_0), .in_2(greaterthan4add3_19_output_1),
    .in_3(greaterthan4add3_19_output_2), .output_0(greaterthan4add3_23_output_0),
    .output_1(greaterthan4add3_23_output_1), .output_2(greaterthan4add3_23_output_2),
    .output_3(greaterthan4add3_23_output_3));
  greaterThan4Add3 greaterthan4add3_24 (
    .in_0(greaterthan4add3_19_output_3), .in_1(greaterthan4add3_20_output_0),
    .in_2(greaterthan4add3_20_output_1), .in_3(greaterthan4add3_20_output_2),
    .output_0(greaterthan4add3_24_output_0), .output_1(greaterthan4add3_24_output_1),
    .output_2(greaterthan4add3_24_output_2), .output_3(greaterthan4add3_24_output_3));
  greaterThan4Add3 greaterthan4add3_25 (
    .in_0(greaterthan4add3_20_output_3), .in_1(greaterthan4add3_21_output_0),
    .in_2(greaterthan4add3_21_output_1), .in_3(greaterthan4add3_21_output_2),
    .output_0(greaterthan4add3_25_output_0), .output_1(greaterthan4add3_25_output_1),
    .output_2(greaterthan4add3_25_output_2), .output_3(greaterthan4add3_25_output_3));
  greaterThan4Add3 greaterthan4add3_26 (
    .in_0(greaterthan4add3_21_output_3), .in_1(greaterthan4add3_22_output_0),
    .in_2(greaterthan4add3_22_output_1), .in_3(greaterthan4add3_22_output_2),
    .output_0(greaterthan4add3_26_output_0), .output_1(greaterthan4add3_26_output_1),
    .output_2(greaterthan4add3_26_output_2), .output_3(greaterthan4add3_26_output_3));
  greaterThan4Add3 greaterthan4add3_27 (
    .in_0(Binary_16bit[2]), .in_1(greaterthan4add3_23_output_0), .in_2(greaterthan4add3_23_output_1),
    .in_3(greaterthan4add3_23_output_2), .output_0(greaterthan4add3_27_output_0),
    .output_1(greaterthan4add3_27_output_1), .output_2(greaterthan4add3_27_output_2),
    .output_3(greaterthan4add3_27_output_3));
  greaterThan4Add3 greaterthan4add3_28 (
    .in_0(greaterthan4add3_23_output_3), .in_1(greaterthan4add3_24_output_0),
    .in_2(greaterthan4add3_24_output_1), .in_3(greaterthan4add3_24_output_2),
    .output_0(greaterthan4add3_28_output_0), .output_1(greaterthan4add3_28_output_1),
    .output_2(greaterthan4add3_28_output_2), .output_3(greaterthan4add3_28_output_3));
  greaterThan4Add3 greaterthan4add3_29 (
    .in_0(greaterthan4add3_24_output_3), .in_1(greaterthan4add3_25_output_0),
    .in_2(greaterthan4add3_25_output_1), .in_3(greaterthan4add3_25_output_2),
    .output_0(greaterthan4add3_29_output_0), .output_1(greaterthan4add3_29_output_1),
    .output_2(greaterthan4add3_29_output_2), .output_3(greaterthan4add3_29_output_3));
  greaterThan4Add3 greaterthan4add3_30 (
    .in_0(greaterthan4add3_25_output_3), .in_1(greaterthan4add3_26_output_0),
    .in_2(greaterthan4add3_26_output_1), .in_3(greaterthan4add3_26_output_2),
    .output_0(greaterthan4add3_30_output_0), .output_1(greaterthan4add3_30_output_1),
    .output_2(greaterthan4add3_30_output_2), .output_3(greaterthan4add3_30_output_3));
  greaterThan4Add3 greaterthan4add3_31 (
    .in_0(Binary_16bit[1]), .in_1(greaterthan4add3_27_output_0), .in_2(greaterthan4add3_27_output_1),
    .in_3(greaterthan4add3_27_output_2), .output_0(BCD_1s[1]), .output_1(BCD_1s[2]), .output_2(BCD_1s[3]),
    .output_3(BCD_10s[0]));
  greaterThan4Add3 greaterthan4add3_32 (
    .in_0(greaterthan4add3_27_output_3), .in_1(greaterthan4add3_28_output_0),
    .in_2(greaterthan4add3_28_output_1), .in_3(greaterthan4add3_28_output_2), .output_0(BCD_10s[1]),
    .output_1(BCD_10s[2]), .output_2(BCD_10s[3]), .output_3(BCD_100s[0]));
  greaterThan4Add3 greaterthan4add3_33 (
    .in_0(greaterthan4add3_28_output_3), .in_1(greaterthan4add3_29_output_0),
    .in_2(greaterthan4add3_29_output_1), .in_3(greaterthan4add3_29_output_2), .output_0(BCD_100s[1]),
    .output_1(BCD_100s[2]), .output_2(BCD_100s[3]), .output_3(BCD_1000s[0]));
  greaterThan4Add3 greaterthan4add3_34 (
    .in_0(greaterthan4add3_29_output_3), .in_1(greaterthan4add3_30_output_0),
    .in_2(greaterthan4add3_30_output_1), .in_3(greaterthan4add3_30_output_2), .output_0(BCD_1000s[1]),
    .output_1(BCD_1000s[2]), .output_2(BCD_1000s[3]), .output_3(BCD_10000s[0]));
  greaterThan4Add3 greaterthan4add3_35 (
    .in_0(greaterthan4add3_30_output_3), .in_1(greaterthan4add3_26_output_3),
    .in_2(greaterthan4add3_22_output_3), .in_3(1'b0), .output_0(BCD_10000s[1]), .output_1(BCD_10000s[2]),
    .output_2(BCD_10000s[3]));  // open: output_3

  assign BCD_1s[0] = Binary_16bit[0];
endmodule
