// Logisim project DisplaySelect.circ as structural Verilog: 1 circuit, main circuit main
module main (
  input  Z_flag,
  output z1,
  output [1:0] DS,
  output z0
);

  wire a0_qn, a1_qn, and_1_out, and_2_out, and_3_out, and_4_out, and_5_out, and_6_out, and_7_out, and_8_out,
       and_9_out, and_10_out, BTNC_out, BTNL_out, BTNR_out, clock_1_out, not_1_out, not_2_out, not_3_out,
       or_1_out, or_2_out;

  Button BTNL (.out(BTNL_out));
  Button BTNR (.out(BTNR_out));
  not not_1 (not_1_out, BTNL_out);
  not not_2 (not_2_out, BTNR_out);
  and and_1 (and_1_out, z1, z0);
  and and_2 (and_2_out, a0_qn, BTNL_out);
  and and_3 (and_3_out, BTNL_out, not_2_out);
  and and_4 (and_4_out, not_2_out, a0_qn);
  and and_5 (and_5_out, a1_qn, BTNR_out);
  and and_6 (and_6_out, a0_qn, BTNR_out, not_1_out);
  and and_7 (and_7_out, a0_qn, and_3_out);
  and and_8 (and_8_out, not_2_out, not_1_out, z0);
  and and_9 (and_9_out, and_1_out, BTNL_out);
  or or_1 (or_1_out, and_1_out, and_2_out, and_3_out, and_4_out);
  or or_2 (or_2_out, and_5_out, and_6_out, and_7_out, and_8_out, and_9_out);
  D_Flip_Flop a1 (.D(or_1_out), .clk(clock_1_out), .Q(z1), .Qn(a1_qn));  // open: preset, reset
  D_Flip_Flop a0 (.D(or_2_out), .clk(clock_1_out), .Q(z0), .Qn(a0_qn));  // open: preset, reset
  Clock clock_1 (.out(clock_1_out));
  and and_10 (and_10_out, not_3_out, Z_flag);
  not not_3 (not_3_out, BTNC_out);
  Button BTNC (.out(BTNC_out));
  Multiplexer #(.width(2)) multiplexer_1 (.in0(2'b00), .in1({z1, z0}), .out(DS), .sel(and_10_out));
endmodule
