// Logisim project DoubleDabble.circ as structural Verilog: 1 circuit, main circuit main
module main (
);

  wire comparator_1_gt, comparator_2_gt, comparator_3_gt, comparator_4_gt, comparator_5_gt, comparator_6_gt,
       comparator_7_gt, comparator_8_gt, comparator_9_gt, comparator_10_gt, comparator_11_gt,
       comparator_12_gt, comparator_13_gt, comparator_14_gt, comparator_15_gt, comparator_16_gt,
       comparator_17_gt, comparator_18_gt, comparator_19_gt, comparator_20_gt, comparator_21_gt,
       comparator_22_gt, comparator_23_gt, comparator_24_gt, comparator_25_gt, comparator_26_gt,
       comparator_27_gt;
  wire [0:0] undriven_2, undriven_3, undriven_4, undriven_6, undriven_8, undriven_9, undriven_10,
       undriven_11, undriven_12;
  wire [2:0] multiplexer_4_out, undriven;
  wire [2:2] multiplexer_5_out_2;
  wire [3:0] adder_1_out, adder_2_out, adder_3_out, adder_4_out, adder_5_out, adder_6_out, adder_7_out,
       adder_8_out, adder_9_out, adder_10_out, adder_11_out, adder_12_out, adder_13_out, adder_14_out,
       adder_15_out, adder_16_out, adder_17_out, adder_18_out, adder_19_out, adder_20_out, adder_21_out,
       adder_22_out, adder_23_out, adder_24_out, adder_25_out, adder_26_out, adder_27_out, multiplexer_1_out,
       multiplexer_2_out, multiplexer_3_out, multiplexer_5_out, multiplexer_6_out, multiplexer_7_out,
       multiplexer_8_out, multiplexer_9_out, multiplexer_10_out, multiplexer_11_out, multiplexer_12_out,
       multiplexer_13_out, multiplexer_14_out, multiplexer_15_out, multiplexer_16_out, multiplexer_17_out,
       multiplexer_18_out, multiplexer_19_out, multiplexer_20_out, multiplexer_21_out, multiplexer_22_out,
       multiplexer_23_out, multiplexer_24_out, multiplexer_25_out, multiplexer_26_out, multiplexer_27_out,
       undriven_7;
  wire [7:7] undriven_5;

  Adder #(.width(4)) adder_1 (.a(4'b0011), .b({1'b0, undriven}), .out(adder_1_out));  // open: cin, cout
  Multiplexer #(.width(4)) multiplexer_1 (
    .in0({1'b0, undriven}), .in1(adder_1_out), .out(multiplexer_1_out), .sel(comparator_1_gt));
  Comparator #(.mode("unsigned"), .width(4)) comparator_1 (
    .a({1'b0, undriven}), .b(4'b0100), .gt(comparator_1_gt));  // open: eq, lt
  Adder #(.width(4)) adder_2 (
    .a(4'b0011), .b({multiplexer_1_out[2:0], undriven_2[0]}), .out(adder_2_out));  // open: cin, cout
  Multiplexer #(.width(4)) multiplexer_2 (
    .in0({multiplexer_1_out[2:0], undriven_2[0]}), .in1(adder_2_out), .out(multiplexer_2_out),
    .sel(comparator_2_gt));
  Comparator #(.mode("unsigned"), .width(4)) comparator_2 (
    .a({multiplexer_1_out[2:0], undriven_2[0]}), .b(4'b0100), .gt(comparator_2_gt));  // open: eq, lt
  Adder #(.width(4)) adder_3 (
    .a(4'b0011), .b({multiplexer_2_out[2:0], undriven_3[0]}), .out(adder_3_out));  // open: cin, cout
  Multiplexer #(.width(4)) multiplexer_3 (
    .in0({multiplexer_2_out[2:0], undriven_3[0]}), .in1(adder_3_out), .out(multiplexer_3_out),
    .sel(comparator_3_gt));
  Comparator #(.mode("unsigned"), .width(4)) comparator_3 (
    .a({multiplexer_2_out[2:0], undriven_3[0]}), .b(4'b0100), .gt(comparator_3_gt));  // open: eq, lt
  Adder #(.width(4)) adder_4 (
    .a(4'b0011), .b({multiplexer_3_out[2:0], undriven_4[0]}), .out(adder_4_out));  // open: cin, cout
  Multiplexer #(.width(4)) multiplexer_4 (
    .in0({multiplexer_3_out[2:0], undriven_4[0]}), .in1(adder_4_out),
    .out({multiplexer_5_out[0], multiplexer_4_out}), .sel(comparator_4_gt));
  Comparator #(.mode("unsigned"), .width(4)) comparator_4 (
    .a({multiplexer_3_out[2:0], undriven_4[0]}), .b(4'b0100), .gt(comparator_4_gt));  // open: eq, lt
  Adder #(.width(4)) adder_5 (
    .a(4'b0011), .b({1'b0, multiplexer_1_out[3], multiplexer_2_out[3], multiplexer_3_out[3]}),
    .out(adder_5_out));  // open: cin, cout
  Comparator #(.mode("unsigned"), .width(4)) comparator_5 (
    .a({1'b0, multiplexer_1_out[3], multiplexer_2_out[3], multiplexer_3_out[3]}), .b(4'b0100),
    .gt(comparator_5_gt));  // open: eq, lt
  Multiplexer #(.width(4)) multiplexer_5 (
    .in0({1'b0, multiplexer_1_out[3], multiplexer_2_out[3], multiplexer_3_out[3]}), .in1(adder_5_out),
    .out({multiplexer_5_out_2[2], multiplexer_5_out[3:1]}), .sel(comparator_5_gt));
  Adder #(.width(4)) adder_6 (
    .a(4'b0011), .b({multiplexer_4_out, undriven_5[7]}), .out(adder_6_out));  // open: cin, cout
  Multiplexer #(.width(4)) multiplexer_6 (
    .in0({multiplexer_4_out, undriven_5[7]}), .in1(adder_6_out), .out(multiplexer_6_out),
    .sel(comparator_6_gt));
  Comparator #(.mode("unsigned"), .width(4)) comparator_6 (
    .a({multiplexer_4_out, undriven_5[7]}), .b(4'b0100), .gt(comparator_6_gt));  // open: eq, lt
  Adder #(.width(4)) adder_7 (.a(4'b0011), .b(multiplexer_5_out), .out(adder_7_out));  // open: cin, cout
  Comparator #(.mode("unsigned"), .width(4)) comparator_7 (
    .a(multiplexer_5_out), .b(4'b0100), .gt(comparator_7_gt));  // open: eq, lt
  Multiplexer #(.width(4)) multiplexer_7 (
    .in0(multiplexer_5_out), .in1(adder_7_out), .out(multiplexer_7_out), .sel(comparator_7_gt));
  Adder #(.width(4)) adder_8 (
    .a(4'b0011), .b({multiplexer_6_out[2:0], undriven_6[0]}), .out(adder_8_out));  // open: cin, cout
  Multiplexer #(.width(4)) multiplexer_8 (
    .in0({multiplexer_6_out[2:0], undriven_6[0]}), .in1(adder_8_out), .out(multiplexer_8_out),
    .sel(comparator_8_gt));
  Comparator #(.mode("unsigned"), .width(4)) comparator_8 (
    .a({multiplexer_6_out[2:0], undriven_6[0]}), .b(4'b0100), .gt(comparator_8_gt));  // open: eq, lt
  Adder #(.width(4)) adder_9 (
    .a(4'b0011), .b({multiplexer_7_out[2:0], multiplexer_6_out[3]}), .out(adder_9_out));  // open: cin, cout
  Comparator #(.mode("unsigned"), .width(4)) comparator_9 (
    .a({multiplexer_7_out[2:0], multiplexer_6_out[3]}), .b(4'b0100), .gt(comparator_9_gt));  // open: eq, lt
  Adder #(.width(4)) adder_10 (.a(4'b0011), .b(undriven_7), .out(adder_10_out));  // open: cin, cout
  Comparator #(.mode("unsigned"), .width(4)) comparator_10 (
    .a(undriven_7), .b(4'b0100), .gt(comparator_10_gt));  // open: eq, lt
  Multiplexer #(.width(4)) multiplexer_9 (
    .in0({multiplexer_7_out[2:0], multiplexer_6_out[3]}), .in1(adder_9_out), .out(multiplexer_9_out),
    .sel(comparator_9_gt));
  Multiplexer #(.width(4)) multiplexer_10 (
    .in0(undriven_7), .in1(adder_10_out), .out(multiplexer_10_out), .sel(comparator_10_gt));
  Adder #(.width(4)) adder_11 (
    .a(4'b0011), .b({multiplexer_8_out[2:0], undriven_8[0]}), .out(adder_11_out));  // open: cin, cout
  Multiplexer #(.width(4)) multiplexer_11 (
    .in0({multiplexer_8_out[2:0], undriven_8[0]}), .in1(adder_11_out), .out(multiplexer_11_out),
    .sel(comparator_11_gt));
  Comparator #(.mode("unsigned"), .width(4)) comparator_11 (
    .a({multiplexer_8_out[2:0], undriven_8[0]}), .b(4'b0100), .gt(comparator_11_gt));  // open: eq, lt
  Adder #(.width(4)) adder_12 (
    .a(4'b0011), .b({multiplexer_9_out[2:0], multiplexer_8_out[3]}), .out(adder_12_out));  // open: cin, cout
  Comparator #(.mode("unsigned"), .width(4)) comparator_12 (
    .a({multiplexer_9_out[2:0], multiplexer_8_out[3]}), .b(4'b0100), .gt(comparator_12_gt));  // open: eq, lt
  Adder #(.width(4)) adder_13 (
    .a(4'b0011), .b({1'b0, multiplexer_5_out_2[2], multiplexer_7_out[3], multiplexer_9_out[3]}),
    .out(adder_13_out));  // open: cin, cout
  Multiplexer #(.width(4)) multiplexer_12 (
    .in0({multiplexer_9_out[2:0], multiplexer_8_out[3]}), .in1(adder_12_out), .out(multiplexer_12_out),
    .sel(comparator_12_gt));
  Multiplexer #(.width(4)) multiplexer_13 (
    .in0({1'b0, multiplexer_5_out_2[2], multiplexer_7_out[3], multiplexer_9_out[3]}), .in1(adder_13_out),
    .out(multiplexer_13_out), .sel(comparator_13_gt));
  Comparator #(.mode("unsigned"), .width(4)) comparator_13 (
    .a({1'b0, multiplexer_5_out_2[2], multiplexer_7_out[3], multiplexer_9_out[3]}), .b(4'b0100),
    .gt(comparator_13_gt));  // open: eq, lt
  Adder #(.width(4)) adder_14 (
    .a(4'b0011), .b({multiplexer_11_out[2:0], undriven_9[0]}), .out(adder_14_out));  // open: cin, cout
  Multiplexer #(.width(4)) multiplexer_14 (
    .in0({multiplexer_11_out[2:0], undriven_9[0]}), .in1(adder_14_out), .out(multiplexer_14_out),
    .sel(comparator_14_gt));
  Comparator #(.mode("unsigned"), .width(4)) comparator_14 (
    .a({multiplexer_11_out[2:0], undriven_9[0]}), .b(4'b0100), .gt(comparator_14_gt));  // open: eq, lt
  Adder #(.width(4)) adder_15 (
    .a(4'b0011), .b({multiplexer_12_out[2:0], multiplexer_11_out[3]}), .out(adder_15_out));  // open: cin, cout
  Comparator #(.mode("unsigned"), .width(4)) comparator_15 (
    .a({multiplexer_12_out[2:0], multiplexer_11_out[3]}), .b(4'b0100), .gt(comparator_15_gt));  // open: eq, lt
  Adder #(.width(4)) adder_16 (
    .a(4'b0011), .b({multiplexer_13_out[2:0], multiplexer_12_out[3]}), .out(adder_16_out));  // open: cin, cout
  Multiplexer #(.width(4)) multiplexer_15 (
    .in0({multiplexer_12_out[2:0], multiplexer_11_out[3]}), .in1(adder_15_out), .out(multiplexer_15_out),
    .sel(comparator_15_gt));
  Multiplexer #(.width(4)) multiplexer_16 (
    .in0({multiplexer_13_out[2:0], multiplexer_12_out[3]}), .in1(adder_16_out), .out(multiplexer_16_out),
    .sel(comparator_16_gt));
  Comparator #(.mode("unsigned"), .width(4)) comparator_16 (
    .a({multiplexer_13_out[2:0], multiplexer_12_out[3]}), .b(4'b0100), .gt(comparator_16_gt));  // open: eq, lt
  Adder #(.width(4)) adder_17 (
    .a(4'b0011), .b({multiplexer_14_out[2:0], undriven_10[0]}), .out(adder_17_out));  // open: cin, cout
  Multiplexer #(.width(4)) multiplexer_17 (
    .in0({multiplexer_14_out[2:0], undriven_10[0]}), .in1(adder_17_out), .out(multiplexer_17_out),
    .sel(comparator_17_gt));
  Comparator #(.mode("unsigned"), .width(4)) comparator_17 (
    .a({multiplexer_14_out[2:0], undriven_10[0]}), .b(4'b0100), .gt(comparator_17_gt));  // open: eq, lt
  Adder #(.width(4)) adder_18 (
    .a(4'b0011), .b({multiplexer_15_out[2:0], multiplexer_14_out[3]}), .out(adder_18_out));  // open: cin, cout
  Comparator #(.mode("unsigned"), .width(4)) comparator_18 (
    .a({multiplexer_15_out[2:0], multiplexer_14_out[3]}), .b(4'b0100), .gt(comparator_18_gt));  // open: eq, lt
  Adder #(.width(4)) adder_19 (
    .a(4'b0011), .b({multiplexer_16_out[2:0], multiplexer_15_out[3]}), .out(adder_19_out));  // open: cin, cout
  Multiplexer #(.width(4)) multiplexer_18 (
    .in0({multiplexer_15_out[2:0], multiplexer_14_out[3]}), .in1(adder_18_out), .out(multiplexer_18_out),
    .sel(comparator_18_gt));
  Multiplexer #(.width(4)) multiplexer_19 (
    .in0({multiplexer_16_out[2:0], multiplexer_15_out[3]}), .in1(adder_19_out), .out(multiplexer_19_out),
    .sel(comparator_19_gt));
  Comparator #(.mode("unsigned"), .width(4)) comparator_19 (
    .a({multiplexer_16_out[2:0], multiplexer_15_out[3]}), .b(4'b0100), .gt(comparator_19_gt));  // open: eq, lt
  Adder #(.width(4)) adder_20 (
    .a(4'b0011), .b({multiplexer_17_out[2:0], undriven_11[0]}), .out(adder_20_out));  // open: cin, cout
  Multiplexer #(.width(4)) multiplexer_20 (
    .in0({multiplexer_17_out[2:0], undriven_11[0]}), .in1(adder_20_out), .out(multiplexer_20_out),
    .sel(comparator_20_gt));
  Comparator #(.mode("unsigned"), .width(4)) comparator_20 (
    .a({multiplexer_17_out[2:0], undriven_11[0]}), .b(4'b0100), .gt(comparator_20_gt));  // open: eq, lt
  Adder #(.width(4)) adder_21 (
    .a(4'b0011), .b({multiplexer_18_out[2:0], multiplexer_17_out[3]}), .out(adder_21_out));  // open: cin, cout
  Comparator #(.mode("unsigned"), .width(4)) comparator_21 (
    .a({multiplexer_18_out[2:0], multiplexer_17_out[3]}), .b(4'b0100), .gt(comparator_21_gt));  // open: eq, lt
  Adder #(.width(4)) adder_22 (
    .a(4'b0011), .b({multiplexer_19_out[2:0], multiplexer_18_out[3]}), .out(adder_22_out));  // open: cin, cout
  Multiplexer #(.width(4)) multiplexer_21 (
    .in0({multiplexer_18_out[2:0], multiplexer_17_out[3]}), .in1(adder_21_out), .out(multiplexer_21_out),
    .sel(comparator_21_gt));
  Multiplexer #(.width(4)) multiplexer_22 (
    .in0({multiplexer_19_out[2:0], multiplexer_18_out[3]}), .in1(adder_22_out), .out(multiplexer_22_out),
    .sel(comparator_22_gt));
  Comparator #(.mode("unsigned"), .width(4)) comparator_22 (
    .a({multiplexer_19_out[2:0], multiplexer_18_out[3]}), .b(4'b0100), .gt(comparator_22_gt));  // open: eq, lt
  Adder #(.width(4)) adder_23 (
    .a(4'b0011), .b({1'b0, multiplexer_13_out[3], multiplexer_16_out[3], multiplexer_19_out[3]}),
    .out(adder_23_out));  // open: cin, cout
  Multiplexer #(.width(4)) multiplexer_23 (
    .in0({1'b0, multiplexer_13_out[3], multiplexer_16_out[3], multiplexer_19_out[3]}), .in1(adder_23_out),
    .out(multiplexer_23_out), .sel(comparator_23_gt));
  Comparator #(.mode("unsigned"), .width(4)) comparator_23 (
    .a({1'b0, multiplexer_13_out[3], multiplexer_16_out[3], multiplexer_19_out[3]}), .b(4'b0100),
    .gt(comparator_23_gt));  // open: eq, lt
  Adder #(.width(4)) adder_24 (
    .a(4'b0011), .b({multiplexer_20_out[2:0], undriven_12[0]}), .out(adder_24_out));  // open: cin, cout
  Multiplexer #(.width(4)) multiplexer_24 (
    .in0({multiplexer_20_out[2:0], undriven_12[0]}), .in1(adder_24_out), .out(multiplexer_24_out),
    .sel(comparator_24_gt));
  Comparator #(.mode("unsigned"), .width(4)) comparator_24 (
    .a({multiplexer_20_out[2:0], undriven_12[0]}), .b(4'b0100), .gt(comparator_24_gt));  // open: eq, lt
  Adder #(.width(4)) adder_25 (
    .a(4'b0011), .b({multiplexer_21_out[2:0], multiplexer_20_out[3]}), .out(adder_25_out));  // open: cin, cout
  Comparator #(.mode("unsigned"), .width(4)) comparator_25 (
    .a({multiplexer_21_out[2:0], multiplexer_20_out[3]}), .b(4'b0100), .gt(comparator_25_gt));  // open: eq, lt
  Adder #(.width(4)) adder_26 (
    .a(4'b0011), .b({multiplexer_22_out[2:0], multiplexer_21_out[3]}), .out(adder_26_out));  // open: cin, cout
  Multiplexer #(.width(4)) multiplexer_25 (
    .in0({multiplexer_21_out[2:0], multiplexer_20_out[3]}), .in1(adder_25_out), .out(multiplexer_25_out),
    .sel(comparator_25_gt));
  Multiplexer #(.width(4)) multiplexer_26 (
    .in0({multiplexer_22_out[2:0], multiplexer_21_out[3]}), .in1(adder_26_out), .out(multiplexer_26_out),
    .sel(comparator_26_gt));
  Comparator #(.mode("unsigned"), .width(4)) comparator_26 (
    .a({multiplexer_22_out[2:0], multiplexer_21_out[3]}), .b(4'b0100), .gt(comparator_26_gt));  // open: eq, lt
  Adder #(.width(4)) adder_27 (
    .a(4'b0011), .b({multiplexer_23_out[2:0], multiplexer_22_out[3]}), .out(adder_27_out));  // open: cin, cout
  Multiplexer #(.width(4)) multiplexer_27 (
    .in0({multiplexer_23_out[2:0], multiplexer_22_out[3]}), .in1(adder_27_out), .out(multiplexer_27_out),
    .sel(comparator_27_gt));
  Comparator #(.mode("unsigned"), .width(4)) comparator_27 (
    .a({multiplexer_23_out[2:0], multiplexer_22_out[3]}), .b(4'b0100), .gt(comparator_27_gt));  // open: eq, lt
endmodule
